# Fritzing sketch diagram (saved by Fritzing 0.9.3b)

parts:
  tft1 = 3.5in tft touch screen
  Part1 = Arduino Uno (Rev3)
  Part2 = sensor_biometrico
  S6 = Pushbutton [package="[SMD]"]
  S7 = Pushbutton [package="[SMD]"]
  S8 = Pushbutton [package="[SMD]"]
  S9 = Pushbutton [package="[SMD]"]
  LED1 = smd LED [color="Red (633nm)" package="0805 [SMD]"]
  LED2 = smd LED [color="Red (633nm)" package="0805 [SMD]"]
  R1 = Resistor [tolerance=±5% resistance=220 package="2010 [SMD]"]
  R2 = Resistor [tolerance=±5% resistance=220 package="2010 [SMD]"]
  J1 = Piezo Speaker
  S10 = Pushbutton [package="[SMD]"]
  S11 = Pushbutton [package="[SMD]"]
  S12 = Pushbutton [package="[SMD]"]
  S13 = Pushbutton [package="[SMD]"]
  ZS-042_RTC1 = ZS-042 RTC Module

nets:
  GND: tft1.GND, Part1.GND, S6.Pin_1, S6.Pin_2, LED1.cathode
  VCC: tft1.VCC, tft1.NC, Part1.5V
  N1: Part1.A0, S6.Pin_3, S6.Pin_4
  N2: Part1.A1, S7.Pin_3, S7.Pin_4
  N3: Part1.A2, S9.Pin_3, S9.Pin_4
  N4: Part1.A3, S8.Pin_3, S8.Pin_4
  N5: Part1.A4/SDA, ZS-042_RTC1.SDA
  N6: Part1.A5/SCL, ZS-042_RTC1.SCL
  N7: Part1.D8, S10.Pin_2
  N8: Part1.D9_PWM, S11.Pin_2
  N9: Part1.D10_PWM/SS, S12.Pin_3, S12.Pin_4
  N10: Part1.D11_PWM/MOSI, S13.Pin_2
  N11: Part1.D2, Part2.TX
  N12: Part1.D3_PWM, Part2.RX
  N13: Part1.D5_PWM, J1.pin2
  N14: Part1.D6_PWM, R2.Pin_1
  N15: Part1.D7, R1.Pin_1
  N16: LED1.anode, R1.Pin_0
  N17: LED2.anode, R2.Pin_0

custom parts:
  3.5in tft touch screen: 3.2" tft touch screen lcd display
  sensor_biometrico: Adafruit Optical Fingerprint Sensor
