# Fritzing sketch fingerprint-schematic-design (saved by Fritzing 0.9.3b)

parts:
  Part2 = Arduino Due (Rev2b)
  S3 = Pushbutton [package="[SMD]"]
  S4 = Pushbutton [package="[SMD]"]
  S5 = Pushbutton [package="[SMD]"]
  S6 = Pushbutton [package="[SMD]"]
  S7 = Pushbutton [package="[SMD]"]
  S8 = Pushbutton [package="[SMD]"]
  S9 = Pushbutton [package="[SMD]"]
  S10 = Pushbutton [package="[SMD]"]
  S11 = Pushbutton [package="[SMD]"]
  R1 = Resistor [tolerance=±5% resistance=220 package="2512 [SMD]"]
  LED1 = LED - 3mm [color="Red (633nm)" package="3 mm [THT]"]
  LED2 = LED - 3mm [color="Green (570nm)" package="3 mm [THT]"]
  R2 = Resistor [tolerance=±5% resistance=220 package="2512 [SMD]"]
  R3 = Resistor [tolerance=±5% resistance=220 package="2512 [SMD]"]
  R4 = Resistor [tolerance=±5% resistance=220 package="2512 [SMD]"]
  LED3 = LED - 3mm [color="Red (633nm)" package="3 mm [THT]"]
  LED4 = LED - 3mm [color="Green (570nm)" package="3 mm [THT]"]
  R5 = Resistor [tolerance=±5% resistance=220 package="2512 [SMD]"]
  R6 = Resistor [tolerance=±5% resistance=220 package="2512 [SMD]"]
  LED5 = LED - 3mm [color="Green (570nm)" package="3 mm [THT]"]
  LED6 = LED - 3mm [color="Red (633nm)" package="3 mm [THT]"]
  R7 = Resistor [tolerance=±5% resistance=220 package="2512 [SMD]"]
  R8 = Resistor [tolerance=±5% resistance=220 package="2512 [SMD]"]
  LED7 = LED - 3mm [color="Green (570nm)" package="3 mm [THT]"]
  LED8 = LED - 3mm [color="Red (633nm)" package="3 mm [THT]"]
  R9 = Resistor [tolerance=±5% resistance=220 package="2512 [SMD]"]
  R10 = Resistor [tolerance=±5% resistance=220 package="2512 [SMD]"]
  LED9 = LED - 3mm [color="Red (633nm)" package="3 mm [THT]"]
  LED10 = LED - 3mm [color="Green (570nm)" package="3 mm [THT]"]
  Part3 = sensor_biometrico
  J1 = Piezo Speaker
  SD_card_module1 = SD Card Module

nets:
  N1: Part2.A8, S11.Pin_3, S11.Pin_4
  N2: Part2.A0, S3.Pin_3, S3.Pin_4
  N3: Part2.A1, S4.Pin_3, S4.Pin_4
  N4: Part2.A2, S6.Pin_3, S6.Pin_4
  N5: Part2.A3, S5.Pin_3, S5.Pin_4
  N6: Part2.A4, S8.Pin_3, S8.Pin_4
  N7: Part2.A5, S10.Pin_3, S10.Pin_4
  GND: Part2.A6, Part2.GND, S3.Pin_1, S3.Pin_2, S4.Pin_1, S4.Pin_2, S5.Pin_2, S6.Pin_1, S6.Pin_2, S7.Pin_1, S7.Pin_2, S8.Pin_2, S9.Pin_2, S9.Pin_3, S9.Pin_4, S10.Pin_2, S11.Pin_1, S11.Pin_2, LED1.cathode, LED2.cathode, LED3.cathode, LED4.cathode, LED5.cathode, LED6.cathode, LED7.cathode, LED8.cathode, LED9.cathode, LED10.cathode, Part3.GND, J1.pin1, SD_card_module1.GND
  N8: Part2.A7, S7.Pin_3, S7.Pin_4
  5V: Part2.5V, Part3.VCC, SD_card_module1.+5
  N9: Part2.D2_PWM, Part3.TX
  N10: Part2.D3_PWM, Part3.RX
  N11: Part2.D5_PWM, J1.pin2
  N12: Part2.D24, R10.Pin_1
  N13: Part2.D26, R9.Pin_1
  N14: Part2.D28, R8.Pin_1
  N15: Part2.D30, R7.Pin_1
  N16: Part2.D32, R6.Pin_1
  N17: Part2.D34, R5.Pin_1
  N18: Part2.D36, R4.Pin_1
  N19: Part2.D38, R3.Pin_1
  N20: Part2.D40, R2.Pin_1
  N21: Part2.D42, R1.Pin_1
  N22: Part2.D50, SD_card_module1.MISO
  N23: Part2.D51, SD_card_module1.MOSI
  N24: Part2.D52, SD_card_module1.SCK
  N25: Part2.D53, SD_card_module1.CS
  N26: R1.Pin_0, LED1.anode
  N27: LED2.anode, R2.Pin_0
  N28: R3.Pin_0, LED4.anode
  N29: R4.Pin_0, LED3.anode
  N30: R5.Pin_0, LED6.anode
  N31: R6.Pin_0, LED5.anode
  N32: R7.Pin_0, LED8.anode
  N33: R8.Pin_0, LED7.anode
  N34: R9.Pin_0, LED9.anode
  N35: R10.Pin_0, LED10.anode

custom parts:
  sensor_biometrico: Adafruit Optical Fingerprint Sensor
  SD Card Module: SD Card Module Slot Socket Reader For Arduino ARM MCU
